# Fritzing sketch Leo (saved by Fritzing 0.9.2b)
breadboards: 1

parts:
  Composant1 = Arduino Leonardo (Rev3b)
  LED1 = RGB LED (com. cathode, rgb) [package="5 mm [THT]"]
  IC1 = L293D [package=THT]
  Composant3 = Adafruit Bluefruit LE SPI Friend [part_number="Adafruit #2633"]
  R1 = Resistor [tolerance=±5% resistance=330 package=THT]
  R2 = Resistor [tolerance=±5% resistance=330 package=THT]
  R3 = Resistor [tolerance=±5% resistance=330 package=THT]
  VCC1 = Battery block 9V
  M1 = DC Motor
  M2 = DC Motor

nets:
  N1: Composant1.D2/SDA, IC1.In_1
  N2: Composant1.D3_PWM/SCL, IC1.Enable_2
  N3: Composant1.D4/A6, IC1.In_2
  N4: Composant1.D5_PWM, IC1.In_3
  N5: Composant1.D6_PWM/A7, IC1.Enable_1
  N6: Composant1.D7, IC1.In_4
  N7: Composant1.5V, IC1.+V
  N8: Composant1.D8/A8, Composant3.RST
  N9: Composant1.D9_PWM/A9, Composant3.IRQ
  N10: Composant1.D10_PWM/A10, R2.Pin_0
  N11: Composant1.D11_PWM, R3.Pin_0
  N12: Composant1.D12/A11, Composant3.CS
  N13: Composant1.D13_PWM, R1.Pin_0
  N14: Composant1.GND, LED1.common_cathode, IC1.0V, VCC1.-
  N15: LED1.red_anode, R1.Pin_1
  N16: LED1.green_anode, R2.Pin_1
  N17: LED1.blue_anode, R3.Pin_1
  N18: IC1.Out_1_(_Controlled_by_Enable_1_), M1.pin_1
  N19: IC1.Out_2_(_Controlled_by_Enable_1_), M1.pin_2
  N20: IC1.+Vmotor, VCC1.+
  N21: IC1.Out_3_(_Controlled_by_Enable_2_), M2.pin_2
  N22: IC1.Out_4_(_Controlled_by_Enable_2_), M2.pin_1

custom parts:
  Adafruit Bluefruit LE SPI Friend: The Bluefruit LE SPI Friend makes it easy to add Bluetooth Low Energy connectivity to anything with 4 or 5 GPIO pins. With SPI, you don't have to worry about baud rates, flow control, or giving up a hardware UART port. Connect to your Arduino or other microcontroller using the common four-pin SPI interface (MISO, MOSI, SCK and CS) plus a 5th GPIO pin for interrupts (to let the Arduino know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
